// Logisim project 32-bit-ALU.circ as structural Verilog: 14 circuits, main circuit main
// ALU
module main (
  input  [1:0] CONTROL,
  input  [31:0] INPUT1,
  input  [31:0] INPUT2,
  output [31:0] RESULT,
  output CARRY,
  output OVERFLOW,
  output zero,
  output SIGN
);

  wire sub_detect_1_output;
  wire [31:0] n32_bit_add_sub_1_result, n32_bit_and_1_output, n32_bit_or_1_output;

  sub_detect sub_detect_1 (.control(CONTROL), .\output (sub_detect_1_output));
  _32_bit_AND u_32_bit_and_1 (.A(INPUT1), .B(INPUT2), .\output (n32_bit_and_1_output));
  _32_bit_OR u_32_bit_or_1 (.A(INPUT1), .B(INPUT2), .\output (n32_bit_or_1_output));
  _32_bit_ADD_SUB u_32_bit_add_sub_1 (
    .A(INPUT1), .B(INPUT2), .OPP(sub_detect_1_output), .Result(n32_bit_add_sub_1_result), .carry(CARRY),
    .Overflow(OVERFLOW));
  Multiplexer #(.select(2), .width(32)) multiplexer_1 (
    .in0(n32_bit_and_1_output), .in1(n32_bit_or_1_output), .in2(n32_bit_add_sub_1_result),
    .in3(n32_bit_add_sub_1_result), .out(RESULT), .sel(CONTROL));  // open: en
  zero_flag_checker zero_flag_checker_1 (.in_1(RESULT), .out_2(zero));
  _31_bit_out u_31_bit_out_1 (.INPUT(RESULT), ._31st_bit(SIGN));

  // Notes on the sheet:
  //   INSTRUCTIONS :-  
  //   00-AND 
  //   01-OR  
  //   10-ADD 
  //               11-SUBTRACT
  //   2207079
endmodule

module _32_bit_AND (
  input  [31:0] A,
  input  [31:0] B,
  output [31:0] \output 
);

  assign \output  = A & B;  // AND_Gate and_1, 32 bits wide

  // Notes on the sheet:
  //   2207079
endmodule

module _32_bit_OR (
  input  [31:0] A,
  input  [31:0] B,
  output [31:0] \output 
);

  assign \output  = A | B;  // OR_Gate or_1, 32 bits wide
endmodule

module _4_bit_CLA (
  input  C0,
  input  P0,
  input  P1,
  input  P2,
  input  P3,
  input  G0,
  input  G1,
  input  G2,
  input  G3,
  output C1,
  output C2,
  output C3,
  output C4
);

  wire and_1_out, and_2_out, and_3_out, and_4_out, and_5_out, and_6_out, and_7_out, and_8_out, and_9_out,
       and_10_out;

  and and_1 (and_1_out, C0, P0);
  or or_1 (C1, and_1_out, G0);
  and and_2 (and_2_out, and_1_out, P1);
  and and_3 (and_3_out, G0, P1);
  and and_4 (and_4_out, and_2_out, P2);
  and and_5 (and_5_out, and_3_out, P2);
  and and_6 (and_6_out, G1, P2);
  and and_7 (and_7_out, and_4_out, P3);
  and and_8 (and_8_out, and_5_out, P3);
  and and_9 (and_9_out, and_6_out, P3);
  and and_10 (and_10_out, G2, P3);
  or or_2 (C2, G1, and_2_out, and_3_out);
  or or_3 (C3, and_4_out, and_5_out, and_6_out, G2);
  or or_4 (C4, and_7_out, and_8_out, and_9_out, and_10_out, G3);

  // Notes on the sheet:
  //   2207079
endmodule

module _4_bit_ADDER (
  input  C_in,
  input  [3:0] B,
  input  [3:0] A,
  output [3:0] Result,
  output carry
);

  wire and_1_out, and_2_out, and_3_out, and_4_out, n4bitcla_1_c1, n4bitcla_1_c2, n4bitcla_1_c3, xor_1_out,
       xor_2_out, xor_3_out, xor_4_out;

  xor xor_1 (xor_1_out, A[0], B[0]);
  and and_1 (and_1_out, A[0], B[0]);
  xor xor_2 (xor_2_out, A[1], B[1]);
  and and_2 (and_2_out, A[1], B[1]);
  xor xor_3 (xor_3_out, A[2], B[2]);
  and and_3 (and_3_out, A[2], B[2]);
  xor xor_4 (xor_4_out, A[3], B[3]);
  and and_4 (and_4_out, A[3], B[3]);
  _4BitCla u_4bitcla_1 (
    .G3(and_4_out), .P3(xor_4_out), .G2(and_3_out), .P2(xor_3_out), .G1(and_2_out), .p1(xor_2_out),
    .G0(and_1_out), .P0(xor_1_out), .C0(C_in), .C4(carry), .C3(n4bitcla_1_c3), .C2(n4bitcla_1_c2),
    .C1(n4bitcla_1_c1));
  xor xor_5 (Result[0], xor_1_out, C_in);
  xor xor_6 (Result[1], xor_2_out, n4bitcla_1_c1);
  xor xor_7 (Result[2], n4bitcla_1_c2, xor_3_out);
  xor xor_8 (Result[3], n4bitcla_1_c3, xor_4_out);

  // Notes on the sheet:
  //   2207079
endmodule

module _32_bit_adder (
  input  C_in,
  input  [31:0] A,
  input  [31:0] B,
  output [31:0] Result,
  output carry
);

  wire n4_bit_adder_1_carry, n4_bit_adder_2_carry, n4_bit_adder_3_carry, n4_bit_adder_4_carry,
       n4_bit_adder_5_carry, n4_bit_adder_6_carry, n4_bit_adder_7_carry;

  _4_bit_ADDER u_4_bit_adder_1 (
    .C_in(C_in), .B(B[3:0]), .A(A[3:0]), .Result(Result[3:0]), .carry(n4_bit_adder_1_carry));
  _4_bit_ADDER u_4_bit_adder_2 (
    .C_in(n4_bit_adder_1_carry), .B(B[7:4]), .A(A[7:4]), .Result(Result[7:4]), .carry(n4_bit_adder_2_carry));
  _4_bit_ADDER u_4_bit_adder_3 (
    .C_in(n4_bit_adder_2_carry), .B(B[11:8]), .A(A[11:8]), .Result(Result[11:8]), .carry(n4_bit_adder_3_carry));
  _4_bit_ADDER u_4_bit_adder_4 (
    .C_in(n4_bit_adder_3_carry), .B(B[15:12]), .A(A[15:12]), .Result(Result[15:12]),
    .carry(n4_bit_adder_4_carry));
  _4_bit_ADDER u_4_bit_adder_5 (
    .C_in(n4_bit_adder_4_carry), .B(B[19:16]), .A(A[19:16]), .Result(Result[19:16]),
    .carry(n4_bit_adder_5_carry));
  _4_bit_ADDER u_4_bit_adder_6 (
    .C_in(n4_bit_adder_5_carry), .B(B[23:20]), .A(A[23:20]), .Result(Result[23:20]),
    .carry(n4_bit_adder_6_carry));
  _4_bit_ADDER u_4_bit_adder_7 (
    .C_in(n4_bit_adder_6_carry), .B(B[27:24]), .A(A[27:24]), .Result(Result[27:24]),
    .carry(n4_bit_adder_7_carry));
  _4_bit_ADDER u_4_bit_adder_8 (
    .C_in(n4_bit_adder_7_carry), .B(B[31:28]), .A(A[31:28]), .Result(Result[31:28]), .carry(carry));

  // Notes on the sheet:
  //   2207079
endmodule

module _32_bit_ADD_SUB (
  input  [31:0] A,
  input  [31:0] B,
  input  OPP,
  output [31:0] Result,
  output carry,
  output Overflow
);

  wire and_1_out, and_2_out, n31_bit_out_1__31st_bit, n31_bit_out_2__31st_bit, n31_bit_out_3__31st_bit,
       not_1_out, not_2_out, not_3_out;
  wire [31:0] bit_extender_1_out, xor_1_out;

  _31_bit_out u_31_bit_out_1 (.INPUT(A), ._31st_bit(n31_bit_out_1__31st_bit));
  _31_bit_out u_31_bit_out_2 (.INPUT(B), ._31st_bit(n31_bit_out_2__31st_bit));
  assign xor_1_out = B ^ bit_extender_1_out;  // XOR_Gate xor_1, 32 bits wide
  assign bit_extender_1_out = {{31{OPP}}, OPP};  // Bit_Extender bit_extender_1
  _32_bit_adder u_32_bit_adder_1 (.C_in(OPP), .A(A), .B(xor_1_out), .Result(Result), .carry(carry));
  not not_1 (not_1_out, n31_bit_out_1__31st_bit);
  not not_2 (not_2_out, n31_bit_out_2__31st_bit);
  _31_bit_out u_31_bit_out_3 (.INPUT(Result), ._31st_bit(n31_bit_out_3__31st_bit));
  not not_3 (not_3_out, n31_bit_out_3__31st_bit);
  and and_1 (and_1_out, not_3_out, n31_bit_out_1__31st_bit, n31_bit_out_2__31st_bit);
  and and_2 (and_2_out, n31_bit_out_3__31st_bit, not_1_out, not_2_out);
  or or_1 (Overflow, and_1_out, and_2_out);

  // Notes on the sheet:
  //   2207079
endmodule

module _31_bit_out (
  input  [31:0] INPUT,
  output _31st_bit
);


  assign _31st_bit = INPUT[31];

  // Notes on the sheet:
  //   2207079
endmodule

module sub_detect (
  input  [1:0] control,
  output \output 
);

  and and_1 (\output , control[0], control[1]);

  // Notes on the sheet:
  //   2207079
endmodule

module zero_flag_checker (
  input  [31:0] in_1,
  output out_2
);

  wire or_1_out;

  or or_1 (or_1_out, in_1[0], in_1[1], in_1[2], in_1[3], in_1[4], in_1[5], in_1[6], in_1[7], in_1[8], in_1[9], in_1[10], in_1[11], in_1[12], in_1[13], in_1[14], in_1[15], in_1[17], in_1[18], in_1[19], in_1[20], in_1[21], in_1[22], in_1[23], in_1[24], in_1[25], in_1[26], in_1[27], in_1[28], in_1[29], in_1[30], in_1[31], in_1[16]);
  not not_1 (out_2, or_1_out);

  // Notes on the sheet:
  //   2207079
endmodule

module sequence_decoder (
  input  Clk,
  input  Reset,
  input  Q0,
  input  Q_1,
  input  [4:0] Count,
  output Cl__A__Q_1,
  output LOad__M__Q__Cnt,
  output Load_A,
  output C0,
  output C1,
  output Shr,
  output Dec_Cnt
);

  wire counter_1_da, counter_1_db, counter_1_dc, nor_1_out, T0, T2, T4, T6, T7;
  wire [2:0] T;

  nor nor_1 (nor_1_out, Count[0], Count[1], Count[2], Count[3], Count[4]);
  Decoder #(.select(3), .enable("false")) decoder_1 (
    .out0(T0), .out1(Cl__A__Q_1), .out2(T2), .out3(C0), .out4(T4), .out5(Dec_Cnt), .out6(T6), .out7(T7),
    .sel(T));
  counter counter_1 (.Q({Q0, Q_1}), .T(T), .C(nor_1_out), .DA(counter_1_da), .DB(counter_1_db), .DC(counter_1_dc));
  D_Flip_Flop d_ff_1 (.clk(Clk), .D(counter_1_da), .Q(T[0]), .reset(Reset));  // open: Qn, preset, en
  D_Flip_Flop d_ff_2 (.clk(Clk), .D(counter_1_db), .Q(T[1]), .reset(Reset));  // open: Qn, preset, en
  D_Flip_Flop d_ff_3 (.clk(Clk), .D(counter_1_dc), .Q(T[2]), .reset(Reset));  // open: Qn, preset, en
  or or_1 (Load_A, C0, T4);
  or or_2 (C1, T4, C0);

  assign LOad__M__Q__Cnt = Cl__A__Q_1;
  assign Shr = Dec_Cnt;

  // Other names for the same wires on the sheet: T1 = Cl__A__Q_1; T3 = C0; T5 = Dec_Cnt

  // Notes on the sheet:
  //   2207079
endmodule

module counter (
  input  [1:0] Q,
  input  [2:0] T,
  input  C,
  output DA,
  output DB,
  output DC
);

  wire and_1_out, and_2_out, and_3_out, and_4_out, and_5_out, or_4_out, or_5_out, Q0, Q1, Q2, Q3, T0, T1, T2,
       T3, T4, T5, T6, T7;

  Decoder #(.select(2), .enable("false")) decoder_1 (.out0(Q0), .out1(Q1), .out2(Q2), .out3(Q3), .sel(Q));
  Decoder #(.select(3), .enable("false")) decoder_2 (
    .out0(T0), .out1(T1), .out2(T2), .out3(T3), .out4(T4), .out5(T5), .out6(T6), .out7(T7), .sel(T));
  or or_1 (DB, T1, and_4_out, T5, T6, T6, T7);
  or or_2 (DC, T5, and_5_out, T3, T4, and_2_out, T7);
  or or_3 (DA, T0, and_3_out, T3, T4, and_1_out, T7);
  and and_1 (and_1_out, T6, C);
  and and_2 (and_2_out, T6, C);
  and and_3 (and_3_out, T2, or_5_out);
  and and_4 (and_4_out, T2, Q2);
  and and_5 (and_5_out, T2, or_4_out);
  or or_4 (or_4_out, Q0, Q1, Q3);
  or or_5 (or_5_out, Q0, Q2, Q3);

  // Notes on the sheet:
  //   2207079
endmodule

module _4BitCla (
  input  G3,
  input  P3,
  input  G2,
  input  P2,
  input  G1,
  input  p1,
  input  G0,
  input  P0,
  input  C0,
  output C4,
  output C3,
  output C2,
  output C1
);

  wire and_1_out, and_2_out, and_3_out, and_4_out, and_5_out, and_6_out, and_7_out, and_8_out, and_9_out,
       and_10_out;

  and and_1 (and_1_out, P3, G2);
  and and_2 (and_2_out, P3, P2, G1);
  and and_3 (and_3_out, P3, P2, p1, G0);
  and and_4 (and_4_out, P3, P2, p1, P0, C0);
  and and_5 (and_5_out, P2, G1);
  and and_6 (and_6_out, P2, p1, G0);
  and and_7 (and_7_out, P2, p1, P0, C0);
  and and_8 (and_8_out, p1, G0);
  and and_9 (and_9_out, p1, C0, P0);
  and and_10 (and_10_out, P0, C0);
  or or_1 (C4, G3, and_1_out, and_2_out, and_3_out, and_4_out);
  or or_2 (C3, G2, and_5_out, and_6_out, and_7_out);
  or or_3 (C2, G1, and_8_out, and_9_out);
  or or_4 (C1, G0, and_10_out);

  // Notes on the sheet:
  //   2207079
endmodule

module control_unit (
  input  [31:0] in_1,
  input  [31:0] in_2,
  input  in_3
);

  wire A_out, clock_1_out, or_1_out, Q_out, Q_q31, sequence_decoder_1_cl__a__q_1, sequence_decoder_1_dec_cnt,
       sequence_decoder_1_load__m__q__cnt, sequence_decoder_1_load_a, sequence_decoder_1_shr,
       shift_register_1_q0;
  wire [1:0] sequence_decoder_1_c0;
  wire [4:0] counter_1_q;
  wire [31:0] A_q31, M_q31, main_1_result;

  Clock clock_1 (.out(clock_1_out));
  sequence_decoder sequence_decoder_1 (
    .Clk(clock_1_out), .Reset(in_3), .Q0(Q_q31), .Q_1(shift_register_1_q0), .Count(counter_1_q),
    .Cl__A__Q_1(sequence_decoder_1_cl__a__q_1), .LOad__M__Q__Cnt(sequence_decoder_1_load__m__q__cnt),
    .Load_A(sequence_decoder_1_load_a), .C0(sequence_decoder_1_c0[0]), .C1(sequence_decoder_1_c0[1]),
    .Shr(sequence_decoder_1_shr), .Dec_Cnt(sequence_decoder_1_dec_cnt));
  or or_1 (or_1_out, sequence_decoder_1_load__m__q__cnt, sequence_decoder_1_dec_cnt);
  Counter #(.width(5), .max('h1f)) counter_1 (
    .load(or_1_out), .D(5'b00101), .count(sequence_decoder_1_dec_cnt), .Q(counter_1_q), .clk(clock_1_out));  // open: carry, clr
  Shift_Register #(.length(32)) A (
    .shift(sequence_decoder_1_shr), .in(A_q31[31]), .clk(clock_1_out), .out(A_out),
    .load(sequence_decoder_1_load_a), .clr(sequence_decoder_1_cl__a__q_1), .d0(main_1_result[31]),
    .q0(A_q31[31]), .d1(main_1_result[30]), .q1(A_q31[30]), .d2(main_1_result[29]), .q2(A_q31[29]),
    .d3(main_1_result[28]), .q3(A_q31[28]), .d4(main_1_result[27]), .q4(A_q31[27]), .d5(main_1_result[26]),
    .q5(A_q31[26]), .d6(main_1_result[25]), .q6(A_q31[25]), .d7(main_1_result[24]), .q7(A_q31[24]),
    .d8(main_1_result[23]), .q8(A_q31[23]), .d9(main_1_result[22]), .q9(A_q31[22]), .d10(main_1_result[21]),
    .q10(A_q31[21]), .d11(main_1_result[20]), .q11(A_q31[20]), .d12(main_1_result[19]), .q12(A_q31[19]),
    .d13(main_1_result[18]), .q13(A_q31[18]), .d14(main_1_result[17]), .q14(A_q31[17]),
    .d15(main_1_result[16]), .q15(A_q31[16]), .d16(main_1_result[15]), .q16(A_q31[15]),
    .d17(main_1_result[14]), .q17(A_q31[14]), .d18(main_1_result[13]), .q18(A_q31[13]),
    .d19(main_1_result[12]), .q19(A_q31[12]), .d20(main_1_result[11]), .q20(A_q31[11]),
    .d21(main_1_result[10]), .q21(A_q31[10]), .d22(main_1_result[9]), .q22(A_q31[9]), .d23(main_1_result[8]),
    .q23(A_q31[8]), .d24(main_1_result[7]), .q24(A_q31[7]), .d25(main_1_result[6]), .q25(A_q31[6]),
    .d26(main_1_result[5]), .q26(A_q31[5]), .d27(main_1_result[4]), .q27(A_q31[4]), .d28(main_1_result[3]),
    .q28(A_q31[3]), .d29(main_1_result[2]), .q29(A_q31[2]), .d30(main_1_result[1]), .q30(A_q31[1]),
    .d31(main_1_result[0]), .q31(A_q31[0]));
  Shift_Register #(.length(32)) M (
    .shift(1'b0), .clk(clock_1_out), .load(sequence_decoder_1_load__m__q__cnt), .d0(in_1[31]),
    .q0(M_q31[31]), .d1(in_1[30]), .q1(M_q31[30]), .d2(in_1[29]), .q2(M_q31[29]), .d3(in_1[28]),
    .q3(M_q31[28]), .d4(in_1[27]), .q4(M_q31[27]), .d5(in_1[26]), .q5(M_q31[26]), .d6(in_1[25]),
    .q6(M_q31[25]), .d7(in_1[24]), .q7(M_q31[24]), .d8(in_1[23]), .q8(M_q31[23]), .d9(in_1[22]),
    .q9(M_q31[22]), .d10(in_1[21]), .q10(M_q31[21]), .d11(in_1[20]), .q11(M_q31[20]), .d12(in_1[19]),
    .q12(M_q31[19]), .d13(in_1[18]), .q13(M_q31[18]), .d14(in_1[17]), .q14(M_q31[17]), .d15(in_1[16]),
    .q15(M_q31[16]), .d16(in_1[15]), .q16(M_q31[15]), .d17(in_1[14]), .q17(M_q31[14]), .d18(in_1[13]),
    .q18(M_q31[13]), .d19(in_1[12]), .q19(M_q31[12]), .d20(in_1[11]), .q20(M_q31[11]), .d21(in_1[10]),
    .q21(M_q31[10]), .d22(in_1[9]), .q22(M_q31[9]), .d23(in_1[8]), .q23(M_q31[8]), .d24(in_1[7]),
    .q24(M_q31[7]), .d25(in_1[6]), .q25(M_q31[6]), .d26(in_1[5]), .q26(M_q31[5]), .d27(in_1[4]),
    .q27(M_q31[4]), .d28(in_1[3]), .q28(M_q31[3]), .d29(in_1[2]), .q29(M_q31[2]), .d30(in_1[1]),
    .q30(M_q31[1]), .d31(in_1[0]), .q31(M_q31[0]));  // open: in, out, clr
  main main_1 (
    .INPUT1(A_q31), .INPUT2(M_q31), .CONTROL(sequence_decoder_1_c0), .RESULT(main_1_result));  // open: CARRY, OVERFLOW, zero, SIGN
  Shift_Register #(.length(32)) Q (
    .shift(sequence_decoder_1_shr), .in(A_out), .clk(clock_1_out), .out(Q_out),
    .load(sequence_decoder_1_load__m__q__cnt), .d0(in_2[31]), .d1(in_2[30]), .d2(in_2[29]), .d3(in_2[28]),
    .d4(in_2[27]), .d5(in_2[26]), .d6(in_2[25]), .d7(in_2[24]), .d8(in_2[23]), .d9(in_2[22]), .d10(in_2[21]),
    .d11(in_2[20]), .d12(in_2[19]), .d13(in_2[18]), .d14(in_2[17]), .d15(in_2[16]), .d16(in_2[15]),
    .d17(in_2[14]), .d18(in_2[13]), .d19(in_2[12]), .d20(in_2[11]), .d21(in_2[10]), .d22(in_2[9]),
    .d23(in_2[8]), .d24(in_2[7]), .d25(in_2[6]), .d26(in_2[5]), .d27(in_2[4]), .d28(in_2[3]), .d29(in_2[2]),
    .d30(in_2[1]), .d31(in_2[0]), .q31(Q_q31));  // open: clr, q0, q1, q2, q3, q4, q5, q6, q7, q8, q9, q10, q11, q12, q13, q14, q15, q16, q17, q18, q19, q20, q21, q22, q23, q24, q25, q26, q27, q28, q29, q30
  Shift_Register #(.length(1)) shift_register_1 (
    .shift(sequence_decoder_1_shr), .in(Q_out), .clk(clock_1_out), .clr(sequence_decoder_1_cl__a__q_1),
    .q0(shift_register_1_q0));  // open: out, load, d0

  // Notes on the sheet:
  //   2207079
endmodule
