// Logisim project CPU.circ as structural Verilog
module control_unit (
  input  clock,
  input  reset,
  input  F,
  input  F_prime,
  input  [3:0] Q,
  output R,
  output W,
  output a1,
  output a2,
  output a3,
  output b1,
  output b2,
  output b3,
  output C1,
  output C2,
  output D1,
  output D2,
  output I1,
  output f1,
  output f2
);

  wire and_14_out, and_15_out, or_1_out, or_2_out, or_3_out, Q0, Q1, Q2, Q3, Q4, Q5, Q6, Q7, T0, T1, T2, T3;
  wire [1:0] counter_1_q;

  Decoder #(.select(2)) decoder_1 (.out0(T0), .out1(T1), .out2(T2), .out3(T3), .sel(counter_1_q));  // open: en
  Counter #(.width(2), .max('h3)) counter_1 (.Q(counter_1_q), .clk(clock), .clr(reset));  // open: load, D, count, carry
  Decoder #(.select(3)) decoder_2 (
    .out0(Q0), .out1(Q1), .out2(Q2), .out3(Q3), .out4(Q4), .out5(Q5), .out6(Q6), .out7(Q7), .sel(Q[2:0]));  // open: en
  or or_1 (or_1_out, Q0, Q1, Q3, Q6);
  or or_2 (or_2_out, Q2, Q3, Q4);
  and and_1 (W, or_2_out, F, T3);
  and and_2 (a1, F, Q0, T3);
  and and_3 (a2, F, Q1, T3);
  and and_4 (a3, F, Q6, T3);
  and and_5 (b1, F, Q2, T2);
  and and_6 (b2, F, Q3, T2);
  and and_7 (b3, F, Q4, T2);
  and and_8 (C1, F_prime, T1);
  and and_9 (C2, Q5, T3);
  and and_10 (D1, F_prime, T0);
  and and_11 (D2, F, T0);
  and and_12 (I1, F_prime, T2);
  or or_3 (or_3_out, Q1, Q2, Q3, Q4, Q0, Q6);
  and and_13 (f2, F, T3);
  and and_14 (and_14_out, F_prime, T1);
  and and_15 (and_15_out, T1, or_1_out, F_prime);
  and and_16 (f1, or_3_out, F_prime, T3);
  or or_4 (R, and_14_out, and_15_out);

  // Notes on the sheet:
  //   2207079
endmodule

module CPU (
  input  reset,
  output clock
);

  wire a1, a2, a3, b1, b2, b3, bz, c1, c2, clock_out, d1, d2, f1, f2, i1, j_k_ff_1_q, j_k_ff_1_qn, loadA,
       loadB, loadpc, main_1_carry, or_1_out, R, s, S_qn, W;
  wire [3:0] ir_1_output;
  wire [4:0] mar, multiplexer_1_out, multiplexer_2_out, pcdata;
  wire [31:0] B, mdata, multiplexer_3_out, multiplexer_4_out, n32_bit_parallel_load_register_1_output, res;

  Multiplexer #(.width(5)) multiplexer_1 (.in0(mar), .in1(B[27:23]), .out(multiplexer_1_out), .sel(c2));  // open: en
  Multiplexer #(.width(5)) multiplexer_2 (.in0(pcdata), .in1(B[27:23]), .out(multiplexer_2_out), .sel(d2));  // open: en
  or or_1 (or_1_out, d1, d2);
  and and_1 (s, R, b1);
  Clock u_clock (.out(clock_out));
  PC pc_1 (.count(c1), .load(loadpc), .\input (multiplexer_1_out), .reset(reset), .clock(clock), .\output (pcdata));
  _5_bit_MAR u_5_bit_mar_1 (.load(or_1_out), .\input (multiplexer_2_out), .clock(clock), .reset(reset), .\output (mar));
  J_K_Flip_Flop j_k_ff_1 (
    .J(f1), .clk(clock_out), .K(f2), .Q(j_k_ff_1_q), .Qn(j_k_ff_1_qn));  // open: preset, en, reset
  IR ir_1 (.LOAD(i1), .Input(B[31:28]), .CLK(clock_out), .RESET(reset), .\output (ir_1_output));
  D_Flip_Flop u_S (.Qn(S_qn), .preset(s), .reset(reset));  // open: clk, D, Q, en
  D_Flip_Flop E (.clk(clock), .D(main_1_carry));  // open: Q, Qn, preset, en, reset
  Multiplexer #(.select(2), .width(32)) multiplexer_3 (
    .in0({27'h5, pcdata}), .in1(mdata), .in2(n32_bit_parallel_load_register_1_output),
    .out(multiplexer_3_out), .sel({b1, R}));  // open: in3, en
  Multiplexer #(.width(32)) multiplexer_4 (.in0(res), .in1(B), .out(multiplexer_4_out), .sel(a3));  // open: en
  and and_2 (clock, S_qn, clock_out);
  _32_bit_MBR u_32_bit_mbr_1 (
    .count(b2), .\input (multiplexer_3_out), .CLK(clock), .RESET(reset), .LOAD(loadB), .\output (B));  // open: carry
  _32_bit_parallel_load_register u_32_bit_parallel_load_register_1 (
    .\input (multiplexer_4_out), .CLK(clock), .RESET(reset), .LOAD(loadA),
    .\output (n32_bit_parallel_load_register_1_output));
  or or_2 (loadA, a1, a2, a3);
  _32_bit_ALU_main main_1 (
    .INPUT1(n32_bit_parallel_load_register_1_output), .INPUT2(B), .CONTROL({a2, a1}), .RESULT(res),
    .CARRY(main_1_carry));  // open: OVERFLOW, zero, SIGN
  control_unit control_unit_1 (
    .clock(clock), .reset(reset), .F(j_k_ff_1_q), .F_prime(j_k_ff_1_qn), .Q(ir_1_output), .R(R), .W(W),
    .a1(a1), .a2(a2), .a3(a3), .b1(b1), .b2(b2), .b3(b3), .C1(c1), .C2(c2), .D1(d1), .D2(d2), .I1(i1),
    .f1(f1), .f2(f2));
  or or_3 (loadpc, c2, b3);
  or or_4 (loadB, b1, R, b3);
  nor nor_1 (bz, B[16], B[31], B[30], B[29], B[28], B[27], B[26], B[25], B[24], B[23], B[22], B[21], B[20], B[19], B[18], B[17], B[15], B[14], B[13], B[12], B[11], B[10], B[9], B[8], B[7], B[6], B[5], B[4], B[3], B[2], B[1], B[0]);
  RAM #(.addrWidth(5), .dataWidth(32), .bus("separate")) ram_1 (
    .addr(mar), .din(B), .data(mdata), .str(W), .clk(clock), .ld(R));  // open: sel, clr

  // Other names for the same wires on the sheet: bad[4:0] = B[27:23]; bop[3:0] = B[31:28]; clk = clock;
  //   sbit[1:0] = {b1, R}

  // Notes on the sheet:
  //   2207079
endmodule
