// Logisim project register.circ as structural Verilog: 12 circuits, main circuit main
module main (
);


  // Notes on the sheet:
  //   2207079
endmodule

module parallel_load_register (
  input  Load,
  input  Input_1,
  input  Input_2,
  input  Input_3,
  input  Input_4,
  input  input_5,
  input  CLK,
  input  RESET,
  output Output_1,
  output Output_2,
  output Output_3,
  output Output_4,
  output Output_5
);

  wire and_1_out, and_2_out, and_3_out, and_4_out, and_5_out, and_6_out, and_7_out, and_8_out, and_9_out,
       and_10_out, not_1_out, not_2_out, or_1_out, or_2_out, or_3_out, or_4_out, or_5_out;

  not not_1 (not_1_out, Load);
  not not_2 (not_2_out, not_1_out);
  and and_1 (and_1_out, Output_1, not_1_out);
  and and_2 (and_2_out, Input_1, not_2_out);
  and and_3 (and_3_out, Output_2, not_1_out);
  and and_4 (and_4_out, Input_2, not_2_out);
  and and_5 (and_5_out, Output_3, not_1_out);
  and and_6 (and_6_out, Input_3, not_2_out);
  and and_7 (and_7_out, Output_4, not_1_out);
  and and_8 (and_8_out, Input_4, not_2_out);
  and and_9 (and_9_out, Output_5, not_1_out);
  and and_10 (and_10_out, input_5, not_2_out);
  or or_1 (or_1_out, and_1_out, and_2_out);
  or or_2 (or_2_out, and_3_out, and_4_out);
  or or_3 (or_3_out, and_5_out, and_6_out);
  or or_4 (or_4_out, and_7_out, and_8_out);
  or or_5 (or_5_out, and_9_out, and_10_out);
  D_Flip_Flop d_ff_1 (.clk(CLK), .D(or_1_out), .Q(Output_1), .reset(RESET));  // open: Qn, preset, en
  D_Flip_Flop d_ff_2 (.clk(CLK), .D(or_2_out), .Q(Output_2), .reset(RESET));  // open: Qn, preset, en
  D_Flip_Flop d_ff_3 (.clk(CLK), .D(or_3_out), .Q(Output_3), .reset(RESET));  // open: Qn, preset, en
  D_Flip_Flop d_ff_4 (.clk(CLK), .D(or_4_out), .Q(Output_4), .reset(RESET));  // open: Qn, preset, en
  D_Flip_Flop d_ff_5 (.clk(CLK), .D(or_5_out), .Q(Output_5), .reset(RESET));  // open: Qn, preset, en

  // Notes on the sheet:
  //   2207079
endmodule

module _32_bit_parallel_load_register (
  input  [31:0] \input ,
  input  CLK,
  input  RESET,
  input  LOAD,
  output [31:0] \output 
);

  _8_bit_parallel_load_register u_8_bit_parallel_load_register_1 (
    .Input(\input [7:0]), .Load(LOAD), .CLK(CLK), .RESET(RESET), .Output(\output [7:0]));
  _8_bit_parallel_load_register u_8_bit_parallel_load_register_2 (
    .Input(\input [15:8]), .Load(LOAD), .CLK(CLK), .RESET(RESET), .Output(\output [15:8]));
  _8_bit_parallel_load_register u_8_bit_parallel_load_register_3 (
    .Input(\input [23:16]), .Load(LOAD), .CLK(CLK), .RESET(RESET), .Output(\output [23:16]));
  _8_bit_parallel_load_register u_8_bit_parallel_load_register_4 (
    .Input(\input [31:24]), .Load(LOAD), .CLK(CLK), .RESET(RESET), .Output(\output [31:24]));

  // Notes on the sheet:
  //   2207079
endmodule

module _8_bit_parallel_load_register (
  input  [7:0] Input,
  input  Load,
  input  CLK,
  input  RESET,
  output [7:0] Output
);

  parallel_load_register parallel_load_register_1 (
    .Load(Load), .Input_1(Input[0]), .Input_2(Input[1]), .Input_3(Input[2]), .Input_4(Input[3]),
    .input_5(CLK), .CLK(RESET), .Output_1(Output[0]), .Output_2(Output[1]), .Output_3(Output[2]),
    .Output_4(Output[3]));  // open: RESET, Output_5
  parallel_load_register parallel_load_register_2 (
    .Load(Load), .Input_1(Input[4]), .Input_2(Input[5]), .Input_3(Input[6]), .Input_4(Input[7]),
    .input_5(CLK), .CLK(RESET), .Output_1(Output[4]), .Output_2(Output[5]), .Output_3(Output[6]),
    .Output_4(Output[7]));  // open: RESET, Output_5

  // Notes on the sheet:
  //   2207079
endmodule

module IR (
  input  LOAD,
  input  [3:0] Input,
  input  CLK,
  input  RESET,
  output [3:0] \output 
);

  wire and_1_out, and_2_out, and_3_out, and_4_out, and_5_out, and_6_out, and_7_out, and_8_out, not_1_out,
       not_2_out, or_1_out, or_2_out, or_3_out, or_4_out;

  not not_1 (not_1_out, LOAD);
  not not_2 (not_2_out, not_1_out);
  and and_1 (and_1_out, \output [0], not_1_out);
  and and_2 (and_2_out, Input[0], not_2_out);
  and and_3 (and_3_out, \output [1], not_1_out);
  and and_4 (and_4_out, Input[1], not_2_out);
  and and_5 (and_5_out, \output [2], not_1_out);
  and and_6 (and_6_out, Input[2], not_2_out);
  and and_7 (and_7_out, \output [3], not_1_out);
  and and_8 (and_8_out, Input[3], not_2_out);
  or or_1 (or_1_out, and_1_out, and_2_out);
  or or_2 (or_2_out, and_3_out, and_4_out);
  or or_3 (or_3_out, and_5_out, and_6_out);
  or or_4 (or_4_out, and_7_out, and_8_out);
  D_Flip_Flop d_ff_1 (.clk(CLK), .D(or_1_out), .Q(\output [0]), .reset(RESET));  // open: Qn, preset, en
  D_Flip_Flop d_ff_2 (.clk(CLK), .D(or_2_out), .Q(\output [1]), .reset(RESET));  // open: Qn, preset, en
  D_Flip_Flop d_ff_3 (.clk(CLK), .D(or_3_out), .Q(\output [2]), .reset(RESET));  // open: Qn, preset, en
  D_Flip_Flop d_ff_4 (.clk(CLK), .D(or_4_out), .Q(\output [3]), .reset(RESET));  // open: Qn, preset, en

  // Notes on the sheet:
  //   2207079
endmodule

module binary_counter (
  input  Count,
  input  LOAD,
  input  [3:0] Input,
  input  RESET,
  input  CLK,
  output [3:0] \output ,
  output CarryOut
);

  wire and_1_out, and_2_out, and_3_out, and_4_out, and_5_out, and_6_out, and_7_out, and_8_out, and_9_out,
       and_10_out, and_11_out, and_12_out, not_1_out, not_2_out, not_3_out, not_4_out, not_5_out, not_6_out,
       or_1_out, or_2_out, or_3_out, or_4_out, or_5_out, or_6_out, or_7_out, or_8_out;

  and and_1 (and_1_out, Count, not_1_out);
  not not_1 (not_1_out, LOAD);
  not not_2 (not_2_out, not_1_out);
  not not_3 (not_3_out, Input[0]);
  not not_4 (not_4_out, Input[1]);
  not not_5 (not_5_out, Input[2]);
  not not_6 (not_6_out, Input[3]);
  and and_2 (and_2_out, not_2_out, Input[0]);
  and and_3 (and_3_out, not_2_out, not_3_out);
  and and_4 (and_4_out, not_2_out, Input[1]);
  and and_5 (and_5_out, not_2_out, not_4_out);
  and and_6 (and_6_out, not_2_out, Input[2]);
  and and_7 (and_7_out, not_2_out, not_5_out);
  and and_8 (and_8_out, not_2_out, Input[3]);
  and and_9 (and_9_out, not_2_out, not_6_out);
  and and_10 (and_10_out, and_1_out, \output [0]);
  and and_11 (and_11_out, and_1_out, \output [0], \output [1]);
  and and_12 (and_12_out, and_1_out, \output [0], \output [1], \output [2]);
  or or_1 (or_1_out, and_2_out, and_1_out);
  or or_2 (or_2_out, and_1_out, and_3_out);
  or or_3 (or_3_out, and_4_out, and_10_out);
  or or_4 (or_4_out, and_10_out, and_5_out);
  or or_5 (or_5_out, and_6_out, and_11_out);
  or or_6 (or_6_out, and_11_out, and_7_out);
  or or_7 (or_7_out, and_8_out, and_12_out);
  or or_8 (or_8_out, and_12_out, and_9_out);
  J_K_Flip_Flop j_k_ff_1 (
    .J(or_1_out), .clk(CLK), .K(or_2_out), .Q(\output [0]), .reset(RESET));  // open: Qn, preset, en
  J_K_Flip_Flop j_k_ff_2 (
    .J(or_3_out), .clk(CLK), .K(or_4_out), .Q(\output [1]), .reset(RESET));  // open: Qn, preset, en
  J_K_Flip_Flop j_k_ff_3 (
    .J(or_5_out), .clk(CLK), .K(or_6_out), .Q(\output [2]), .reset(RESET));  // open: Qn, preset, en
  J_K_Flip_Flop j_k_ff_4 (
    .J(or_7_out), .clk(CLK), .K(or_8_out), .Q(\output [3]), .reset(RESET));  // open: Qn, preset, en
  and and_13 (CarryOut, \output [3], \output [2], \output [1], \output [0], and_1_out);

  // Notes on the sheet:
  //   2207079
endmodule

module PC (
  input  count,
  input  load,
  input  [4:0] \input ,
  input  reset,
  input  clock,
  output [4:0] \output 
);

  wire and_1_out, and_2_out, and_3_out, binary_counter_1_carryout, not_1_out, not_2_out, or_1_out, or_2_out;

  binary_counter binary_counter_1 (
    .Count(count), .LOAD(load), .Input(\input [3:0]), .RESET(reset), .CLK(clock), .\output (\output [3:0]),
    .CarryOut(binary_counter_1_carryout));
  not not_1 (not_1_out, load);
  and and_1 (and_1_out, \input [4], load);
  not not_2 (not_2_out, \input [4]);
  and and_2 (and_2_out, not_2_out, load);
  and and_3 (and_3_out, not_1_out, binary_counter_1_carryout);
  or or_1 (or_1_out, and_1_out, and_3_out);
  or or_2 (or_2_out, and_2_out, and_3_out);
  J_K_Flip_Flop j_k_ff_1 (
    .J(or_1_out), .clk(clock), .K(or_2_out), .Q(\output [4]), .reset(reset));  // open: Qn, preset, en

  // Notes on the sheet:
  //   2207079
endmodule

// MBR
module _32_bit_MBR (
  input  count,
  input  [31:0] \input ,
  input  CLK,
  input  RESET,
  input  LOAD,
  output [31:0] \output ,
  output carry
);

  wire n8_bit_counter_1_carry, n8_bit_counter_2_carry, n8_bit_counter_3_carry;

  _8_bit_counter u_8_bit_counter_1 (
    .count(count), .\input (\input [7:0]), .load(LOAD), .clock(CLK), .reset(RESET), .\output (\output [7:0]),
    .carry(n8_bit_counter_1_carry));
  _8_bit_counter u_8_bit_counter_2 (
    .count(n8_bit_counter_1_carry), .\input (\input [15:8]), .load(LOAD), .clock(CLK), .reset(RESET),
    .\output (\output [15:8]), .carry(n8_bit_counter_2_carry));
  _8_bit_counter u_8_bit_counter_3 (
    .count(n8_bit_counter_2_carry), .\input (\input [23:16]), .load(LOAD), .clock(CLK), .reset(RESET),
    .\output (\output [23:16]), .carry(n8_bit_counter_3_carry));
  _8_bit_counter u_8_bit_counter_4 (
    .count(n8_bit_counter_3_carry), .\input (\input [31:24]), .load(LOAD), .clock(CLK), .reset(RESET),
    .\output (\output [31:24]), .carry(carry));
endmodule

module _8_bit_counter (
  input  count,
  input  [7:0] \input ,
  input  load,
  input  clock,
  input  reset,
  output [7:0] \output ,
  output carry
);

  wire binary_counter_1_carryout;

  binary_counter binary_counter_1 (
    .Count(count), .LOAD(load), .Input(\input [3:0]), .RESET(reset), .CLK(clock), .\output (\output [3:0]),
    .CarryOut(binary_counter_1_carryout));
  binary_counter binary_counter_2 (
    .Count(binary_counter_1_carryout), .LOAD(load), .Input(\input [7:4]), .RESET(reset), .CLK(clock),
    .\output (\output [7:4]), .CarryOut(carry));
endmodule

// MAR
module _5_bit_MAR (
  input  load,
  input  [4:0] \input ,
  input  clock,
  input  reset,
  output [4:0] \output 
);

  parallel_load_register parallel_load_register_1 (
    .Load(load), .Input_1(\input [0]), .Input_2(\input [1]), .Input_3(\input [2]), .Input_4(\input [3]),
    .input_5(\input [4]), .CLK(clock), .RESET(reset), .Output_1(\output [0]), .Output_2(\output [1]),
    .Output_3(\output [2]), .Output_4(\output [3]), .Output_5(\output [4]));
endmodule

module AC (
  input  LOAD,
  input  [31:0] in_2,
  input  in_3,
  input  Reset,
  output [31:0] out_5
);

  _4_bit_parallel_load u_4_bit_parallel_load_1 (
    .in_2(in_2[7:4]), .CLK(in_3), .CLR(Reset), .LOAD(LOAD), .out_5(out_5[7:4]));
  _4_bit_parallel_load u_4_bit_parallel_load_2 (
    .in_2(in_2[11:8]), .CLK(in_3), .CLR(Reset), .LOAD(LOAD), .out_5(out_5[11:8]));
  _4_bit_parallel_load u_4_bit_parallel_load_3 (
    .in_2(in_2[15:12]), .CLK(in_3), .CLR(Reset), .LOAD(LOAD), .out_5(out_5[15:12]));
  _4_bit_parallel_load u_4_bit_parallel_load_4 (
    .in_2(in_2[19:16]), .CLK(in_3), .CLR(Reset), .LOAD(LOAD), .out_5(out_5[19:16]));
  _4_bit_parallel_load u_4_bit_parallel_load_5 (
    .in_2(in_2[23:20]), .CLK(in_3), .CLR(Reset), .LOAD(LOAD), .out_5(out_5[23:20]));
  _4_bit_parallel_load u_4_bit_parallel_load_6 (
    .in_2(in_2[27:24]), .CLK(in_3), .CLR(Reset), .LOAD(LOAD), .out_5(out_5[27:24]));
  _4_bit_parallel_load u_4_bit_parallel_load_7 (
    .in_2(in_2[3:0]), .CLK(in_3), .CLR(Reset), .LOAD(LOAD), .out_5(out_5[3:0]));
  _4_bit_parallel_load u_4_bit_parallel_load_8 (
    .in_2(in_2[31:28]), .CLK(in_3), .CLR(Reset), .LOAD(LOAD), .out_5(out_5[31:28]));
endmodule

module _4_bit_parallel_load (
  input  LOAD,
  input  [3:0] in_2,
  input  CLK,
  input  CLR,
  output [3:0] out_5
);

  wire and_1_out, and_2_out, and_3_out, and_4_out, and_5_out, and_6_out, and_7_out, and_8_out, not_1_out,
       not_2_out, not_3_out, not_4_out;

  not not_1 (not_1_out, in_2[0]);
  not not_2 (not_2_out, in_2[2]);
  not not_3 (not_3_out, in_2[3]);
  and and_1 (and_1_out, in_2[0], LOAD);
  and and_2 (and_2_out, not_1_out, LOAD);
  and and_3 (and_3_out, in_2[1], LOAD);
  not not_4 (not_4_out, in_2[1]);
  and and_4 (and_4_out, not_4_out, LOAD);
  and and_5 (and_5_out, in_2[2], LOAD);
  and and_6 (and_6_out, not_2_out, LOAD);
  and and_7 (and_7_out, in_2[3], LOAD);
  and and_8 (and_8_out, not_3_out, LOAD);
  J_K_Flip_Flop j_k_ff_1 (.J(and_1_out), .clk(CLK), .K(and_2_out), .Q(out_5[0]), .reset(CLR));  // open: Qn, preset, en
  J_K_Flip_Flop j_k_ff_2 (.J(and_3_out), .clk(CLK), .K(and_4_out), .Q(out_5[1]), .reset(CLR));  // open: Qn, preset, en
  J_K_Flip_Flop j_k_ff_3 (.J(and_5_out), .clk(CLK), .K(and_6_out), .Q(out_5[2]), .reset(CLR));  // open: Qn, preset, en
  J_K_Flip_Flop j_k_ff_4 (.J(and_7_out), .clk(CLK), .K(and_8_out), .Q(out_5[3]), .reset(CLR));  // open: Qn, preset, en
endmodule
